// Digital circuit ALU.dig as structural Verilog
module ALU (
  input  en_A,
  input  en_B,
  input  en_C,
  input  bus_in,
  input  C,
  output bus_out
);

  wire A_q, B_q, nand_1_out;

  Register A (.D(bus_in), .C(C), .en(en_A), .Q(A_q));
  Register B (.D(bus_in), .C(C), .en(en_B), .Q(B_q));
  nand nand_1 (nand_1_out, A_q, B_q);
  assign bus_out = en_C ? nand_1_out : 1'bz;  // Driver driver_1
endmodule
