// Digital circuit CPU.dig as structural Verilog
module CPU (
  input  CLK
);

  wire alu_1_bus_out, button_1_out, cu_1_en_a, cu_1_en_b, cu_1_en_c, cu_1_ld, cu_1_str, cu_1_working;
  wire [7:0] cu_1_a;

  CU cu_1 (
    .A(cu_1_a), .en_A(cu_1_en_a), .en_B(cu_1_en_b), .en_C(cu_1_en_c), .ld(cu_1_ld), .str(cu_1_str), .C(CLK),
    .working(cu_1_working), .reset(button_1_out));
  ALU alu_1 (
    .en_A(cu_1_en_a), .en_B(cu_1_en_b), .en_C(cu_1_en_c), .bus_out(alu_1_bus_out), .bus_in(alu_1_bus_out),
    .C(CLK));
  LED led_1 (.in(cu_1_working));
  Button button_1 (.out(button_1_out));
  PullDown pulldown_1 (.out(alu_1_bus_out));
  RAMDualPort #(.AddrBits(8)) ramdualport_1 (
    .A(cu_1_a), .Din(alu_1_bus_out), .str(cu_1_str), .C(CLK), .ld(cu_1_ld), .D(alu_1_bus_out));

  // Notes on the sheet:
  //   CLK: Hz: 1000
endmodule
