// Digital circuit CU.dig as structural Verilog
module CU (
  input  C,
  input  reset,
  output [7:0] A,
  output en_A,
  output en_B,
  output en_C,
  output str,
  output ld,
  output working
);

  wire [1:0] counter_1_out;
  wire [5:5] rom_2_d;
  wire [7:0] PC_out;
  wire [24:0] rom_1_d;

  Counter #(.Bits(8)) PC (.en(rom_2_d[5]), .C(C), .clr(reset), .out(PC_out));  // open: ovf
  ROM #(.AddrBits(8), .isProgramMemory("true"), .Bits(25)) rom_1 (.A(PC_out), .sel(1'b1), .D(rom_1_d));
  not not_1 (working, rom_1_d[24]);
  // Probe on rom_1_d
  Counter #(.Bits(2)) counter_1 (.en(1'b1), .C(C), .clr(reset), .out(counter_1_out));  // open: ovf
  Multiplexer #(.Selector_Bits(2), .Bits(8)) multiplexer_1 (
    .sel(counter_1_out), .in_0(rom_1_d[7:0]), .in_1(rom_1_d[15:8]), .in_2(rom_1_d[23:16]), .in_3({8{1'b0}}),
    .out(A));
  ROM #(.isProgramMemory("true"), .Bits(6)) rom_2 (
    .A(counter_1_out), .sel(working), .D({rom_2_d[5], str, ld, en_C, en_B, en_A}));
  PullDown #(.Bits(6)) pulldown_1 (.out({rom_2_d[5], str, ld, en_C, en_B, en_A}));

  // Notes on the sheet:
  //   rom_1 loads program.hex
  //   contents of rom_2 (hex, n*v repeats v):
  //   9,a,14,20
endmodule
